# Fritzing sketch counter_7seg (saved by Fritzing 0.9.6b)
breadboards: 1

parts:
  Arduino = Arduino Uno (Rev3) - ICSP
  S1 = Pushbutton [package="[THT]"]
  S2 = Pushbutton [package="[THT]"]
  7_Segment = 7 Segment Display
  R9 = Resistor [tolerance=±5% power=0.25 resistance=1k package=THT]
  R10 = Resistor [tolerance=±5% power=0.25 resistance=1k package=THT]
  R13 = Resistor [tolerance=±5% power=0.25 resistance=1k package=THT]
  R11 = Resistor [tolerance=±5% power=0.25 resistance=1k package=THT]
  R14 = Resistor [tolerance=±5% power=0.25 resistance=1k package=THT]
  R15 = Resistor [tolerance=±5% power=0.25 resistance=1k package=THT]
  R16 = Resistor [tolerance=±5% power=0.25 resistance=1k package=THT]

nets:
  N1: Arduino.GND, S1.Pin_3, S1.Pin_4, S2.Pin_3, S2.Pin_4
  N2: Arduino.D8, R10.Pin_0
  N3: Arduino.D9_PWM, S2.Pin_1, S2.Pin_2
  N4: Arduino.D10_PWM/SS, S1.Pin_1, S1.Pin_2
  N5: Arduino.D2, R11.Pin_1
  N6: Arduino.D3_PWM, R13.Pin_1
  N7: Arduino.D4, R16.Pin_1
  N8: Arduino.D5_PWM, R14.Pin_0
  N9: Arduino.D6_PWM, R15.Pin_0
  N10: Arduino.D7, R9.Pin_0
  N11: 7_Segment.Segment_E, R15.Pin_1
  N12: 7_Segment.Segment_D, R14.Pin_1
  N13: 7_Segment.Segment_C, R16.Pin_0
  N14: 7_Segment.Segment_B, R13.Pin_0
  N15: 7_Segment.Segment_A, R11.Pin_0
  N16: 7_Segment.Segment_F, R9.Pin_1
  N17: 7_Segment.Segment_G, R10.Pin_1
